# Fritzing sketch Schematics (saved by Fritzing 0.8.7b)
breadboards: 1

parts:
  Arduino_LiliyPad1 = Arduino LilyPad
  LED1 = smd LED [color="Red (633nm)" package="0603 [SMD]"]
  LED2 = LED - 5mm [color="Red (633nm)" package="5 mm [THT]"]
  LED3 = smd LED [color="Red (633nm)" package="0603 [SMD]"]
  R1 = Resistor [tolerance=±10% resistance=1k package=THT]
  UFreq = eab9ae19e78d924315e2f0b5956ff7e2_20_hs_1.5mm_0.508mm [chip_label=IC]
  UVolume = eab9ae19e78d924315e2f0b5956ff7e2_20_hs_1.5mm_0.508mm [chip_label=IC]
  SP1 = SPEAKER [package=pcb_mount_speaker]

nets:
  N1: Arduino_LiliyPad1.GND, Arduino_LiliyPad1.D6, R1.Pin_1, UFreq.connector3, UVolume.connector2, UVolume.connector3
  N2: Arduino_LiliyPad1.D12, UFreq.connector2
  N3: Arduino_LiliyPad1.D11, UFreq.connector1
  N4: Arduino_LiliyPad1.D10, SP1.+
  N5: Arduino_LiliyPad1.D9, SP1.-
  N6: Arduino_LiliyPad1.D5, UVolume.connector1
  N7: Arduino_LiliyPad1.D3, LED1.anode, LED2.anode, LED3.anode
  N8: Arduino_LiliyPad1.POW, UFreq.connector0, UVolume.connector0
  N9: LED1.cathode, LED2.cathode, LED3.cathode, R1.Pin_0
